// Logisim project Abacus_8.circ as structural Verilog: 7 circuits, main circuit main
module main (
);

  wire and_1_out, and_2_out, buffer_1_out, buffer_2_out, buffer_3_out, buffer_4_out, CLK_out, CONTROL_axi,
       CONTROL_axo, CONTROL_axs, CONTROL_cu_axi, CONTROL_cu_axo, CONTROL_cu_axs, CONTROL_cu_flag_a,
       CONTROL_cu_flag_c, CONTROL_cu_flag_e, CONTROL_cu_flag_z, CONTROL_cu_halt, CONTROL_cu_iae,
       CONTROL_cu_ias, CONTROL_cu_irs, CONTROL_cu_mae, CONTROL_cu_mde, CONTROL_cu_mdo, CONTROL_cu_pcc,
       CONTROL_cu_pcd, CONTROL_cu_pce, CONTROL_cu_pcs, CONTROL_cu_ready, CONTROL_cu_rr, CONTROL_cu_rw,
       CONTROL_cu_spc, CONTROL_cu_spe, CONTROL_cu_spi, CONTROL_cu_txo, CONTROL_cu_txs, CONTROL_iae,
       CONTROL_ias, CONTROL_irs, CONTROL_mae, CONTROL_mde, CONTROL_mdo, CONTROL_pcc, CONTROL_pcd,
       CONTROL_pce, CONTROL_pcs, CONTROL_rr, CONTROL_rw, CONTROL_spc, CONTROL_spe, CONTROL_spi, CONTROL_txo,
       CONTROL_txs, not_1_out, not_2_out, not_3_out, pull_resistor_3_node, pull_resistor_4_node, RESET_out;
  wire [2:0] CONTROL_alu_ops;
  wire [3:0] ARITHMETIC_flag, AX_led_lsb, AX_led_msb, CONTROL_cu_clockstep, IA_led_lsb, IA_led_msb,
       IR_led_lsb, IR_led_msb, PC_led_lsb, PC_led_msb, SP_led_lsb, SP_led_msb, TX_led_lsb, TX_led_msb;
  wire [7:0] ARITHMETIC_x, AX_q, buffer_5_out, controlled_buffer_1_out, controlled_buffer_2_out,
       controlled_buffer_4_out, controlled_buffer_6_out, controlled_buffer_8_out, IA_q, IR_q, PC_q,
       pull_resistor_1_node, SP_q, TX_q;

  and and_1 (and_1_out, CONTROL_mde, CONTROL_mdo);
  assign controlled_buffer_1_out = and_1_out ? pull_resistor_1_node : 8'bz;  // Controlled_Buffer controlled_buffer_1
  assign controlled_buffer_2_out = and_2_out ? controlled_buffer_1_out : 8'bz;  // Controlled_Buffer controlled_buffer_2
  and and_2 (and_2_out, CONTROL_mde, not_1_out);
  not not_1 (not_1_out, CONTROL_mdo);
  Button RESET (.out(RESET_out));
  Clock CLK (.out(CLK_out));
  regs_8 IR (
    .D(controlled_buffer_1_out), .S(CONTROL_irs), .Clk(CLK_out), .LED_MSB(IR_led_msb), .LED_LSB(IR_led_lsb),
    .Q(IR_q));  // open: Reset
  Hex_Digit_Display #(.decimalPoint("false")) hex_digit_display_1 (.value(IR_led_msb));
  Hex_Digit_Display #(.decimalPoint("false")) hex_digit_display_2 (.value(IR_led_lsb));
  assign controlled_buffer_1_out = CONTROL_txo ? TX_q : 8'bz;  // Controlled_Buffer controlled_buffer_3
  regs_8 TX (
    .D(controlled_buffer_1_out), .S(CONTROL_txs), .Clk(CLK_out), .Reset(RESET_out), .LED_MSB(TX_led_msb),
    .LED_LSB(TX_led_lsb), .Q(TX_q));
  Hex_Digit_Display #(.decimalPoint("false")) hex_digit_display_3 (.value(TX_led_msb));
  Hex_Digit_Display #(.decimalPoint("false")) hex_digit_display_4 (.value(TX_led_lsb));
  LED led_1 (.in(CONTROL_cu_irs));
  LED led_2 (.in(CONTROL_cu_pcs));
  Pull_Resistor pull_resistor_1 (.node(pull_resistor_1_node));
  Pull_Resistor pull_resistor_2 (.node(controlled_buffer_2_out));
  buf buffer_1 (buffer_1_out, buffer_2_out);
  buf buffer_2 (buffer_2_out, buffer_3_out);
  buf buffer_3 (buffer_3_out, buffer_4_out);
  buf buffer_4 (buffer_4_out, CONTROL_rw);
  LED led_3 (.in(CONTROL_cu_mae));
  LED led_4 (.in(CONTROL_cu_mde));
  LED led_5 (.in(CONTROL_cu_mdo));
  LED led_6 (.in(CONTROL_cu_rr));
  LED led_7 (.in(CONTROL_cu_pcd));
  LED led_8 (.in(CONTROL_cu_spc));
  LED led_9 (.in(CONTROL_cu_spe));
  LED led_10 (.in(CONTROL_cu_spi));
  alu ARITHMETIC (
    .Op(CONTROL_alu_ops), .A(TX_q), .B(controlled_buffer_1_out), .X(ARITHMETIC_x), .Flag(ARITHMETIC_flag));
  RAM #(.trigger("high")) MEMORY (
    .addr(controlled_buffer_6_out), .we(buffer_1_out), .oe(CONTROL_rr), .din(buffer_5_out),
    .dout(pull_resistor_1_node));
  assign buffer_5_out = controlled_buffer_2_out;  // Buffer buffer_5, 8 bits wide
  LED led_11 (.in(CONTROL_cu_rw));
  LED led_12 (.in(CONTROL_cu_ias));
  LED led_13 (.in(CONTROL_cu_iae));
  LED led_14 (.in(CONTROL_cu_pcc));
  LED led_15 (.in(CONTROL_cu_txs));
  LED led_16 (.in(CONTROL_cu_txo));
  LED led_17 (.in(CONTROL_cu_axs));
  LED led_18 (.in(CONTROL_cu_axo));
  LED led_19 (.in(CONTROL_cu_pce));
  ctrl CONTROL (
    .Flags(ARITHMETIC_flag), .Inst(IR_q), .Clk(CLK_out), .Reset(RESET_out), .CU_IRS(CONTROL_cu_irs),
    .IRS(CONTROL_irs), .CU_MAE(CONTROL_cu_mae), .MAE(CONTROL_mae), .CU_MDE(CONTROL_cu_mde),
    .MDE(CONTROL_mde), .CU_MDO(CONTROL_cu_mdo), .MDO(CONTROL_mdo), .CU_RR(CONTROL_cu_rr), .RR(CONTROL_rr),
    .CU_RW(CONTROL_cu_rw), .RW(CONTROL_rw), .CU_IAS(CONTROL_cu_ias), .IAS(CONTROL_ias),
    .CU_IAE(CONTROL_cu_iae), .IAE(CONTROL_iae), .CU_PCC(CONTROL_cu_pcc), .PCC(CONTROL_pcc),
    .CU_PCE(CONTROL_cu_pce), .PCE(CONTROL_pce), .CU_PCS(CONTROL_cu_pcs), .PCS(CONTROL_pcs),
    .CU_PCD(CONTROL_cu_pcd), .PCD(CONTROL_pcd), .CU_SPC(CONTROL_cu_spc), .SPC(CONTROL_spc),
    .CU_SPE(CONTROL_cu_spe), .SPE(CONTROL_spe), .CU_SPI(CONTROL_cu_spi), .SPI(CONTROL_spi),
    .CU_TXS(CONTROL_cu_txs), .TXS(CONTROL_txs), .CU_TXO(CONTROL_cu_txo), .TXO(CONTROL_txo),
    .CU_AXS(CONTROL_cu_axs), .AXS(CONTROL_axs), .CU_AXO(CONTROL_cu_axo), .AXO(CONTROL_axo),
    .CU_AXI(CONTROL_cu_axi), .AXI(CONTROL_axi), .CU_Flag_C(CONTROL_cu_flag_c), .CU_Flag_A(CONTROL_cu_flag_a),
    .CU_Flag_E(CONTROL_cu_flag_e), .CU_Flag_Z(CONTROL_cu_flag_z), .CU_Ready(CONTROL_cu_ready),
    .CU_Halt(CONTROL_cu_halt), .CU_Clockstep(CONTROL_cu_clockstep), .ALU_Ops(CONTROL_alu_ops));
  LED led_20 (.in(CONTROL_cu_axi));
  Hex_Digit_Display #(.decimalPoint("false")) hex_digit_display_5 (.value(CONTROL_cu_clockstep));
  LED led_21 (.in(CONTROL_cu_ready));
  LED led_22 (.in(CONTROL_cu_halt));
  LED led_23 (.in(CONTROL_cu_flag_c));
  not not_2 (not_2_out, CLK_out);
  not not_3 (not_3_out, CONTROL_axi);
  regs_8 AX (
    .D(controlled_buffer_4_out), .S(CONTROL_axs), .Clk(CLK_out), .Reset(RESET_out), .LED_MSB(AX_led_msb),
    .LED_LSB(AX_led_lsb), .Q(AX_q));
  assign controlled_buffer_4_out = not_3_out ? ARITHMETIC_x : 8'bz;  // Controlled_Buffer controlled_buffer_4
  Hex_Digit_Display #(.decimalPoint("false")) hex_digit_display_6 (.value(AX_led_msb));
  regs_8 IA (
    .D(controlled_buffer_1_out), .S(CONTROL_ias), .Clk(CLK_out), .Reset(RESET_out), .LED_MSB(IA_led_msb),
    .LED_LSB(IA_led_lsb), .Q(IA_q));
  Hex_Digit_Display #(.decimalPoint("false")) hex_digit_display_7 (.value(IA_led_msb));
  LED led_24 (.in(CONTROL_cu_flag_a));
  LED led_25 (.in(CONTROL_cu_flag_e));
  LED led_26 (.in(CONTROL_cu_flag_z));
  Pull_Resistor #(.pull(1)) pull_resistor_3 (.node(pull_resistor_3_node));
  assign controlled_buffer_4_out = CONTROL_axi ? controlled_buffer_1_out : 8'bz;  // Controlled_Buffer controlled_buffer_5
  Hex_Digit_Display #(.decimalPoint("false")) hex_digit_display_8 (.value(AX_led_lsb));
  Hex_Digit_Display #(.decimalPoint("false")) hex_digit_display_9 (.value(IA_led_lsb));
  assign controlled_buffer_6_out = CONTROL_mae ? controlled_buffer_8_out : 8'bz;  // Controlled_Buffer controlled_buffer_6
  assign controlled_buffer_1_out = CONTROL_axo ? AX_q : 8'bz;  // Controlled_Buffer controlled_buffer_7
  assign controlled_buffer_8_out = CONTROL_iae ? IA_q : 8'bz;  // Controlled_Buffer controlled_buffer_8
  Pull_Resistor pull_resistor_4 (.node(pull_resistor_4_node));
  Hex_Digit_Display #(.decimalPoint("false")) hex_digit_display_10 (.value(SP_led_msb));
  Hex_Digit_Display #(.decimalPoint("false")) hex_digit_display_11 (.value(PC_led_msb));
  ctrs_8_p SP (
    .Reset(RESET_out), .Set(pull_resistor_4_node), .Inc(CONTROL_spi), .Enb(CONTROL_spc), .Clk(not_2_out),
    .LED_MSB(SP_led_msb), .LED_LSB(SP_led_lsb), .Q(SP_q));
  Hex_Digit_Display #(.decimalPoint("false")) hex_digit_display_12 (.value(SP_led_lsb));
  assign controlled_buffer_1_out = CONTROL_pcd ? PC_q : 8'bz;  // Controlled_Buffer controlled_buffer_9
  ctrs_8 PC (
    .Reset(RESET_out), .Set(CONTROL_pcs), .Inc(pull_resistor_3_node), .Enb(CONTROL_pcc), .Clk(not_2_out),
    .D(controlled_buffer_1_out), .LED_MSB(PC_led_msb), .LED_LSB(PC_led_lsb), .Q(PC_q));
  Hex_Digit_Display #(.decimalPoint("false")) hex_digit_display_13 (.value(PC_led_lsb));
  Pull_Resistor pull_resistor_5 (.node(SP_q));
  assign controlled_buffer_8_out = CONTROL_spe ? SP_q : 8'bz;  // Controlled_Buffer controlled_buffer_10
  Pull_Resistor pull_resistor_6 (.node(PC_q));
  assign controlled_buffer_8_out = CONTROL_pce ? PC_q : 8'bz;  // Controlled_Buffer controlled_buffer_11

  // Notes on the sheet:
  //   MEMORY DATA BUFFER
  //   MEMORY ADDR BUFFER
endmodule

module alu (
  input  [7:0] A,
  input  [7:0] B,
  input  [2:0] Op,
  output [7:0] X,
  output [3:0] Flag
);

  wire and_1_out, and_2_out, and_3_out, and_4_out, and_6_out, and_7_out, and_8_out, or_2_out, or_3_out;
  wire [7:0] adder_1_out, and_5_out, bit_extender_1_out, multiplier_1_out, not_1_out, or_1_out, xor_1_out,
       xor_2_out;

  Pull_Resistor pull_resistor_1 (.node(A));
  Pull_Resistor pull_resistor_2 (.node(B));
  Pull_Resistor pull_resistor_3 (.node(Op));
  and and_1 (and_1_out, ~Op[0], ~Op[1], ~Op[2]);  // AND_Gate
  and and_2 (and_2_out, Op[0], ~Op[1], ~Op[2]);  // AND_Gate
  assign xor_1_out = bit_extender_1_out ^ B;  // XOR_Gate xor_1, 8 bits wide
  and and_3 (and_3_out, ~Op[0], Op[1], ~Op[2]);  // AND_Gate
  and and_4 (and_4_out, ~Op[0], ~Op[1], Op[2]);  // AND_Gate
  assign and_5_out = A & B;  // AND_Gate and_5, 8 bits wide
  and and_6 (and_6_out, Op[0], ~Op[1], Op[2]);  // AND_Gate
  assign or_1_out = A | B;  // OR_Gate or_1, 8 bits wide
  and and_7 (and_7_out, ~Op[0], Op[1], Op[2]);  // AND_Gate
  assign xor_2_out = A ^ B;  // XOR_Gate xor_2, 8 bits wide
  and and_8 (and_8_out, Op[0], Op[1], Op[2]);
  assign not_1_out = ~B;  // NOT_Gate not_1, 8 bits wide
  Comparator comparator_1 (.a(A), .b(B), .gt(Flag[2]), .eq(Flag[1]));  // open: lt
  assign bit_extender_1_out = {{7{and_2_out}}, and_2_out};  // Bit_Extender bit_extender_1
  or or_2 (or_2_out, and_2_out, and_1_out);
  assign X = or_2_out ? adder_1_out : 8'bz;  // Controlled_Buffer controlled_buffer_1
  Adder adder_1 (.a(A), .b(xor_1_out), .out(adder_1_out), .cin(and_2_out), .cout(Flag[3]));
  assign X = and_3_out ? multiplier_1_out : 8'bz;  // Controlled_Buffer controlled_buffer_2
  Multiplier multiplier_1 (.a(A), .b(B), .out(multiplier_1_out));  // open: cin, cout
  assign X = and_4_out ? and_5_out : 8'bz;  // Controlled_Buffer controlled_buffer_3
  assign X = and_6_out ? or_1_out : 8'bz;  // Controlled_Buffer controlled_buffer_4
  assign X = and_7_out ? xor_2_out : 8'bz;  // Controlled_Buffer controlled_buffer_5
  assign X = and_8_out ? not_1_out : 8'bz;  // Controlled_Buffer controlled_buffer_6
  or or_3 (or_3_out, A[0], A[1], A[2], A[3], A[5], A[6], A[7], A[4]);
  not not_2 (Flag[0], or_3_out);
  Pull_Resistor pull_resistor_4 (.node(X));
endmodule

module regs_8 (
  input  [7:0] D,
  input  S,
  input  Clk,
  input  Reset,
  output [3:0] LED_MSB,
  output [3:0] LED_LSB,
  output [7:0] Q
);

  Register #(.trigger("high")) register_1 (.D(D), .en(S), .clk(Clk), .Q({LED_MSB, LED_LSB}), .clr(Reset));

  assign Q = {LED_MSB, LED_LSB};
endmodule

module ctrs_8 (
  input  Reset,
  input  Set,
  input  Inc,
  input  Enb,
  input  Clk,
  input  [7:0] D,
  output [3:0] LED_MSB,
  output [3:0] LED_LSB,
  output [7:0] Q
);

  Counter counter_1 (
    .clr(Reset), .load(Set), .up(Inc), .count(Enb), .clk(Clk), .D(D), .Q({LED_MSB, LED_LSB}));  // open: carry

  assign Q = {LED_MSB, LED_LSB};
endmodule

module ctrl (
  input  [3:0] Flags,
  input  [7:0] Inst,
  input  Clk,
  input  Reset,
  output CU_Ready,
  output CU_Halt,
  output CU_Flag_C,
  output CU_Flag_A,
  output CU_Flag_E,
  output [3:0] CU_Clockstep,
  output CU_Flag_Z,
  output [2:0] ALU_Ops,
  output CU_IRS,
  output CU_MAE,
  output CU_MDE,
  output CU_MDO,
  output CU_RR,
  output CU_RW,
  output CU_IAS,
  output CU_IAE,
  output CU_PCC,
  output CU_PCE,
  output CU_PCS,
  output CU_PCD,
  output CU_SPC,
  output CU_SPE,
  output CU_SPI,
  output CU_TXS,
  output CU_TXO,
  output CU_AXS,
  output CU_AXO,
  output CU_AXI,
  output IRS,
  output MAE,
  output MDE,
  output MDO,
  output RR,
  output RW,
  output IAS,
  output IAE,
  output PCC,
  output PCE,
  output PCS,
  output PCD,
  output SPC,
  output SPE,
  output SPI,
  output TXS,
  output TXO,
  output AXS,
  output AXO,
  output AXI
);

  wire and_1_out, and_2_out, and_3_out, and_4_out, and_5_out, and_6_out, and_7_out, and_8_out, and_9_out,
       and_10_out, and_11_out, and_12_out, and_13_out, and_14_out, and_15_out, and_16_out, and_17_out,
       and_18_out, and_20_out, and_21_out, and_22_out, and_23_out, and_24_out, and_25_out, and_26_out,
       and_27_out, and_28_out, and_29_out, and_30_out, and_31_out, and_32_out, and_33_out, and_34_out,
       and_35_out, and_36_out, and_37_out, and_38_out, and_39_out, and_40_out, and_41_out, and_42_out,
       and_43_out, and_44_out, and_45_out, and_46_out, and_47_out, and_48_out, and_49_out, and_50_out,
       and_51_out, and_52_out, and_53_out, and_54_out, and_55_out, and_56_out, and_57_out, and_58_out,
       and_60_out, and_61_out, and_62_out, and_63_out, and_64_out, and_65_out, and_66_out, and_67_out,
       and_69_out, and_70_out, and_71_out, and_80_out, and_81_out, and_82_out, and_83_out, and_84_out,
       and_85_out, and_86_out, and_87_out, buffer_1_out, buffer_2_out, buffer_3_out, buffer_4_out,
       buffer_5_out, buffer_6_out, buffer_7_out, buffer_8_out, buffer_9_out, buffer_10_out, buffer_11_out,
       buffer_12_out, decoder_1_out0, decoder_1_out1, decoder_1_out2, decoder_1_out3, decoder_2_out2,
       decoder_2_out3, decoder_2_out4, decoder_2_out5, decoder_2_out7, decoder_3_out0, decoder_3_out1,
       decoder_3_out2, decoder_3_out3, decoder_3_out4, decoder_3_out5, decoder_3_out6, decoder_3_out7,
       decoder_3_out8, decoder_3_out9, decoder_3_out10, decoder_3_out11, decoder_3_out12, decoder_3_out13,
       decoder_3_out14, decoder_3_out15, not_1_out, not_2_out, not_3_out, not_4_out, not_5_out, not_6_out,
       not_7_out, not_8_out, not_9_out, not_10_out, or_1_out, or_2_out, or_3_out, or_5_out, or_6_out,
       or_7_out, or_19_out, pull_resistor_1_node, pull_resistor_2_node;
  wire [2:0] and_72_out;
  wire [3:0] and_76_out;
  wire [8:8] or_4_out;

  Register #(.width(4)) register_1 (
    .D(Flags), .en(or_1_out), .clk(Clk), .Q({CU_Flag_C, CU_Flag_A, CU_Flag_E, CU_Flag_Z}), .clr(Reset));
  or or_1 (or_1_out, and_1_out, and_2_out);
  or or_2 (or_2_out, and_10_out, and_11_out, and_12_out, and_13_out, and_14_out, and_15_out, and_16_out, and_17_out, and_4_out, and_5_out);
  and and_1 (and_1_out, decoder_2_out4, or_5_out);
  and and_2 (and_2_out, or_6_out, decoder_2_out2);
  and and_3 (and_3_out, Inst[4], Inst[5], Inst[6], not_1_out);
  not not_1 (not_1_out, Inst[7]);
  S_R_Flip_Flop #(.trigger("high")) s_r_ff_1 (
    .S(and_3_out), .R(Reset), .clk(pull_resistor_1_node), .Q(CU_Halt), .Qn(CU_Ready));  // open: reset, preset
  Pull_Resistor #(.pull(1)) pull_resistor_1 (.node(pull_resistor_1_node));
  Decoder #(.select(2)) decoder_1 (
    .out0(decoder_1_out0), .out1(decoder_1_out1), .out2(decoder_1_out2), .out3(decoder_1_out3),
    .sel(Inst[2:1]), .en(Inst[3]));
  and and_4 (and_4_out, or_5_out, decoder_2_out5);
  and and_5 (and_5_out, or_6_out, decoder_2_out4);
  and and_6 (and_6_out, decoder_1_out0, CU_Flag_C);
  and and_7 (and_7_out, decoder_1_out1, CU_Flag_A);
  and and_8 (and_8_out, decoder_1_out2, CU_Flag_E);
  and and_9 (and_9_out, decoder_1_out3, CU_Flag_Z);
  and and_10 (and_10_out, decoder_3_out0, decoder_2_out3);
  and and_11 (and_11_out, decoder_3_out1, decoder_2_out3);
  and and_12 (and_12_out, decoder_3_out2, decoder_2_out5);
  and and_13 (and_13_out, decoder_3_out3, decoder_2_out3);
  and and_14 (and_14_out, decoder_3_out4, decoder_2_out5);
  and and_15 (and_15_out, decoder_3_out5, decoder_2_out5);
  and and_16 (and_16_out, decoder_3_out6, decoder_2_out7);
  and and_17 (and_17_out, decoder_3_out7, decoder_2_out7);
  Counter #(.max('h7), .trigger("falling"), .width(3)) counter_1 (
    .clr(or_3_out), .load(or_3_out), .up(pull_resistor_2_node), .count(pull_resistor_2_node),
    .clk(and_18_out), .Q(CU_Clockstep[2:0]));  // open: D, carry
  or or_3 (or_3_out, or_2_out, Reset);
  Pull_Resistor #(.pull(1)) pull_resistor_2 (.node(pull_resistor_2_node));
  and and_18 (and_18_out, Clk, CU_Ready);
  or or_4 (or_4_out[8], and_6_out, and_7_out, and_8_out, and_9_out);
  Decoder #(.enable("false"), .select(3)) decoder_2 (
    .out2(decoder_2_out2), .out3(decoder_2_out3), .out4(decoder_2_out4), .out5(decoder_2_out5),
    .out7(decoder_2_out7), .sel(CU_Clockstep[2:0]));  // open: out0, out1, out6
  or or_5 (or_5_out, decoder_3_out8, decoder_3_out9, decoder_3_out10, decoder_3_out11);
  or or_6 (or_6_out, decoder_3_out12, decoder_3_out13, decoder_3_out14, decoder_3_out15);
  Decoder #(.enable("false"), .select(4)) decoder_3 (
    .out0(decoder_3_out0), .out1(decoder_3_out1), .out2(decoder_3_out2), .out3(decoder_3_out3),
    .out4(decoder_3_out4), .out5(decoder_3_out5), .out6(decoder_3_out6), .out7(decoder_3_out7),
    .out8(decoder_3_out8), .out9(decoder_3_out9), .out10(decoder_3_out10), .out11(decoder_3_out11),
    .out12(decoder_3_out12), .out13(decoder_3_out13), .out14(decoder_3_out14), .out15(decoder_3_out15),
    .sel(Inst[7:4]));
  Pull_Resistor pull_resistor_3 (.node(CU_Clockstep));
  not not_2 (not_2_out, or_4_out[8]);
  not not_3 (not_3_out, Inst[7]);
  Pull_Resistor pull_resistor_4 (.node(or_4_out[8]));
  Pull_Resistor pull_resistor_5 (.node(not_2_out));
  Pull_Resistor pull_resistor_6 (.node(Inst[7]));
  Pull_Resistor pull_resistor_7 (.node(not_3_out));
  Pull_Resistor pull_resistor_8 (.node(Inst[6]));
  not not_4 (not_4_out, Inst[6]);
  not not_5 (not_5_out, Inst[5]);
  not not_6 (not_6_out, Inst[4]);
  Pull_Resistor pull_resistor_9 (.node(not_4_out));
  Pull_Resistor pull_resistor_10 (.node(Inst[5]));
  Pull_Resistor pull_resistor_11 (.node(not_5_out));
  Pull_Resistor pull_resistor_12 (.node(Inst[4]));
  Pull_Resistor pull_resistor_13 (.node(not_6_out));
  not not_7 (not_7_out, CU_Clockstep[2]);
  not not_8 (not_8_out, CU_Clockstep[1]);
  not not_9 (not_9_out, Inst[3]);
  Pull_Resistor pull_resistor_14 (.node(not_7_out));
  Pull_Resistor pull_resistor_15 (.node(CU_Clockstep[1]));
  Pull_Resistor pull_resistor_16 (.node(not_8_out));
  Pull_Resistor pull_resistor_17 (.node(Inst[3]));
  Pull_Resistor pull_resistor_18 (.node(not_9_out));
  Pull_Resistor pull_resistor_19 (.node(CU_Clockstep[2]));
  not not_10 (not_10_out, CU_Clockstep[0]);
  and and_19 (CU_IRS, not_10_out, not_8_out, not_7_out);
  and and_20 (and_20_out, not_6_out, not_5_out, not_4_out, not_3_out);
  and and_21 (and_21_out, CU_Clockstep[0], not_8_out, not_7_out);
  and and_22 (and_22_out, not_10_out, CU_Clockstep[1], not_7_out);
  and and_23 (and_23_out, Inst[4], not_5_out, not_4_out, not_3_out);
  and and_24 (and_24_out, CU_Clockstep[0], not_8_out, not_7_out);
  and and_25 (and_25_out, not_10_out, CU_Clockstep[1], not_7_out);
  and and_26 (and_26_out, not_6_out, Inst[5], not_4_out, not_3_out);
  and and_27 (and_27_out, CU_Clockstep[0], not_8_out, not_7_out);
  and and_28 (and_28_out, not_10_out, CU_Clockstep[1], not_7_out);
  and and_29 (and_29_out, CU_Clockstep[0], CU_Clockstep[1], not_7_out);
  and and_30 (and_30_out, not_10_out, not_8_out, CU_Clockstep[2]);
  and and_31 (and_31_out, not_9_out, Inst[4], Inst[5], not_4_out, not_3_out);
  and and_32 (and_32_out, Inst[3], Inst[4], Inst[5], not_4_out, not_3_out);
  and and_33 (and_33_out, CU_Clockstep[0], not_8_out, not_7_out);
  and and_34 (and_34_out, not_10_out, CU_Clockstep[1], not_7_out);
  and and_35 (and_35_out, Inst[3], Inst[4], Inst[5], not_4_out, not_3_out);
  and and_36 (and_36_out, CU_Clockstep[0], not_8_out, not_7_out);
  and and_37 (and_37_out, not_10_out, CU_Clockstep[1], not_7_out);
  and and_38 (and_38_out, not_9_out, not_6_out, not_5_out, Inst[6], not_3_out);
  and and_39 (and_39_out, CU_Clockstep[0], not_8_out, not_7_out);
  and and_40 (and_40_out, not_10_out, CU_Clockstep[1], not_7_out);
  and and_41 (and_41_out, CU_Clockstep[0], CU_Clockstep[1], not_7_out);
  and and_42 (and_42_out, not_10_out, not_8_out, CU_Clockstep[2]);
  and and_43 (and_43_out, not_9_out, Inst[4], not_5_out, Inst[6], not_3_out);
  and and_44 (and_44_out, CU_Clockstep[0], not_8_out, not_7_out);
  and and_45 (and_45_out, not_10_out, CU_Clockstep[1], not_7_out);
  and and_46 (and_46_out, CU_Clockstep[0], CU_Clockstep[1], not_7_out);
  and and_47 (and_47_out, not_10_out, not_8_out, CU_Clockstep[2]);
  and and_48 (and_48_out, not_4_out, Inst[7]);
  and and_49 (and_49_out, CU_Clockstep[0], not_8_out, not_7_out);
  and and_50 (and_50_out, not_10_out, CU_Clockstep[1], not_7_out);
  and and_51 (and_51_out, CU_Clockstep[0], CU_Clockstep[1], not_7_out);
  and and_52 (and_52_out, not_10_out, not_8_out, CU_Clockstep[2]);
  and and_53 (and_53_out, Inst[6], Inst[7]);
  and and_54 (and_54_out, CU_Clockstep[0], not_8_out, not_7_out);
  and and_55 (and_55_out, not_10_out, CU_Clockstep[1], not_7_out);
  and and_56 (and_56_out, CU_Clockstep[0], CU_Clockstep[1], not_7_out);
  and and_57 (and_57_out, Inst[4], Inst[5], not_4_out, Inst[7]);
  Pull_Resistor pull_resistor_20 (.node(CU_Clockstep[0]));
  Pull_Resistor pull_resistor_21 (.node(not_10_out));
  and and_58 (and_58_out, and_20_out, and_21_out);
  and and_59 (AXI, and_20_out, and_22_out);
  and and_60 (and_60_out, and_23_out, and_24_out);
  and and_61 (and_61_out, and_23_out, and_25_out);
  and and_62 (and_62_out, and_26_out, and_27_out);
  and and_63 (and_63_out, and_26_out, and_28_out);
  and and_64 (and_64_out, and_26_out, and_29_out);
  and and_65 (and_65_out, and_26_out, and_30_out);
  or or_7 (or_7_out, and_31_out, and_66_out);
  and and_66 (and_66_out, and_32_out, or_4_out[8]);
  and and_67 (and_67_out, or_7_out, and_33_out);
  and and_68 (CU_PCS, or_7_out, and_34_out);
  and and_69 (and_69_out, and_35_out, not_2_out);
  and and_70 (and_70_out, and_69_out, and_36_out);
  and and_71 (and_71_out, and_69_out, and_37_out);
  and and_72 (and_72_out[0], and_38_out, and_39_out);
  and and_73 (and_72_out[1], and_38_out, and_40_out);
  and and_74 (and_72_out[2], and_38_out, and_41_out);
  and and_75 (CU_SPI, and_38_out, and_42_out);
  and and_76 (and_76_out[0], and_43_out, and_44_out);
  and and_77 (and_76_out[1], and_43_out, and_45_out);
  and and_78 (and_76_out[2], and_43_out, and_46_out);
  and and_79 (and_76_out[3], and_43_out, and_47_out);
  and and_80 (and_80_out, and_48_out, and_49_out);
  and and_81 (and_81_out, and_48_out, and_50_out);
  and and_82 (and_82_out, and_48_out, and_51_out);
  and and_83 (and_83_out, and_48_out, and_52_out);
  and and_84 (and_84_out, and_53_out, and_54_out);
  and and_85 (and_85_out, and_53_out, and_55_out);
  and and_86 (and_86_out, and_53_out, and_56_out);
  and and_87 (and_87_out, and_57_out, and_52_out);
  or or_8 (CU_MAE, CU_IRS, and_58_out, AXI, and_60_out, and_61_out, and_62_out, and_63_out, and_64_out, and_65_out, and_67_out, and_72_out[0], and_72_out[1], and_72_out[2], and_76_out[0], and_76_out[1], and_76_out[2], and_80_out, and_81_out, and_82_out, and_83_out, and_85_out, and_86_out);
  or or_9 (CU_MDO, CU_IRS, and_58_out, AXI, and_60_out, and_62_out, and_63_out, and_64_out, and_67_out, and_72_out[0], and_72_out[1], and_76_out[0], and_76_out[1], and_80_out, and_81_out, and_82_out, and_83_out, and_85_out, and_86_out);
  buf buffer_1 (buffer_1_out, and_72_out[2]);
  buf buffer_2 (buffer_2_out, buffer_1_out);
  or or_10 (CU_RW, and_61_out, and_65_out, buffer_2_out, buffer_4_out);
  buf buffer_3 (buffer_3_out, and_76_out[2]);
  buf buffer_4 (buffer_4_out, buffer_3_out);
  or or_11 (CU_IAS, and_58_out, and_60_out, and_62_out, and_64_out, and_72_out[0], and_76_out[0], and_80_out, and_82_out, and_85_out);
  buf buffer_5 (buffer_5_out, and_76_out[2]);
  buf buffer_6 (buffer_6_out, buffer_5_out);
  or or_12 (CU_IAE, AXI, and_61_out, and_63_out, and_65_out, and_72_out[1], buffer_6_out, and_81_out, and_83_out, and_86_out);
  or or_13 (CU_PCC, CU_IRS, and_58_out, and_60_out, and_62_out, and_64_out, and_67_out, CU_PCS, and_71_out, and_72_out[0], and_76_out[0], and_80_out, and_82_out, and_85_out);
  or or_14 (CU_PCE, CU_IRS, and_58_out, and_60_out, and_62_out, and_64_out, and_67_out, and_72_out[0], and_76_out[0], and_80_out, and_82_out, and_85_out);
  Pull_Resistor pull_resistor_22 (.node(CU_PCD));
  or or_15 (CU_SPC, CU_SPI, and_76_out[0]);
  buf buffer_7 (buffer_7_out, and_72_out[2]);
  buf buffer_8 (buffer_8_out, buffer_7_out);
  or or_16 (CU_SPE, buffer_8_out, and_76_out[1]);
  or or_17 (CU_TXS, and_63_out, and_67_out, and_72_out[1], and_76_out[1], and_81_out, and_84_out);
  buf buffer_9 (buffer_9_out, and_72_out[2]);
  buf buffer_10 (buffer_10_out, buffer_9_out);
  or or_18 (CU_TXO, and_65_out, CU_PCS, buffer_10_out, buffer_12_out);
  buf buffer_11 (buffer_11_out, and_76_out[2]);
  buf buffer_12 (buffer_12_out, buffer_11_out);
  or or_19 (or_19_out, AXI, and_83_out, and_86_out);
  and and_88 (AXS, ~and_87_out, or_19_out);  // AND_Gate
  or or_20 (AXO, and_61_out, and_84_out);

  assign ALU_Ops = Inst[6:4];
  assign CU_AXI = AXI;
  assign CU_AXO = AXO;
  assign CU_AXS = AXS;
  assign CU_MDE = CU_MAE;
  assign CU_RR = CU_MDO;
  assign IAE = CU_IAE;
  assign IAS = CU_IAS;
  assign IRS = CU_IRS;
  assign MAE = CU_MAE;
  assign MDE = CU_MAE;
  assign MDO = CU_MDO;
  assign PCC = CU_PCC;
  assign PCD = CU_PCD;
  assign PCE = CU_PCE;
  assign PCS = CU_PCS;
  assign RR = CU_MDO;
  assign RW = CU_RW;
  assign SPC = CU_SPC;
  assign SPE = CU_SPE;
  assign SPI = CU_SPI;
  assign TXO = CU_TXO;
  assign TXS = CU_TXS;
endmodule

module test (
  input  [7:0] in_1
);

  wire CLK_out, CONTROL_cu_axi, CONTROL_cu_axo, CONTROL_cu_axs, CONTROL_cu_flag_a, CONTROL_cu_flag_c,
       CONTROL_cu_flag_e, CONTROL_cu_flag_z, CONTROL_cu_halt, CONTROL_cu_iae, CONTROL_cu_ias, CONTROL_cu_irs,
       CONTROL_cu_mae, CONTROL_cu_mde, CONTROL_cu_mdo, CONTROL_cu_pcc, CONTROL_cu_pcd, CONTROL_cu_pce,
       CONTROL_cu_pcs, CONTROL_cu_ready, CONTROL_cu_rr, CONTROL_cu_rw, CONTROL_cu_spc, CONTROL_cu_spe,
       CONTROL_cu_spi, CONTROL_cu_txo, CONTROL_cu_txs, RESET_out;
  wire [3:0] CONTROL_cu_clockstep;

  Button RESET (.out(RESET_out));
  Clock CLK (.out(CLK_out));
  LED led_1 (.in(CONTROL_cu_irs));
  LED led_2 (.in(CONTROL_cu_mae));
  LED led_3 (.in(CONTROL_cu_mde));
  LED led_4 (.in(CONTROL_cu_mdo));
  LED led_5 (.in(CONTROL_cu_pcs));
  LED led_6 (.in(CONTROL_cu_pcd));
  LED led_7 (.in(CONTROL_cu_spc));
  LED led_8 (.in(CONTROL_cu_spe));
  LED led_9 (.in(CONTROL_cu_rr));
  LED led_10 (.in(CONTROL_cu_rw));
  LED led_11 (.in(CONTROL_cu_ias));
  LED led_12 (.in(CONTROL_cu_iae));
  LED led_13 (.in(CONTROL_cu_spi));
  LED led_14 (.in(CONTROL_cu_txs));
  LED led_15 (.in(CONTROL_cu_txo));
  LED led_16 (.in(CONTROL_cu_axs));
  LED led_17 (.in(CONTROL_cu_pcc));
  LED led_18 (.in(CONTROL_cu_pce));
  ctrl CONTROL (
    .Inst(in_1), .Clk(CLK_out), .Reset(RESET_out), .CU_IRS(CONTROL_cu_irs), .CU_MAE(CONTROL_cu_mae),
    .CU_MDE(CONTROL_cu_mde), .CU_MDO(CONTROL_cu_mdo), .CU_RR(CONTROL_cu_rr), .CU_RW(CONTROL_cu_rw),
    .CU_IAS(CONTROL_cu_ias), .CU_IAE(CONTROL_cu_iae), .CU_PCC(CONTROL_cu_pcc), .CU_PCE(CONTROL_cu_pce),
    .CU_PCS(CONTROL_cu_pcs), .CU_PCD(CONTROL_cu_pcd), .CU_SPC(CONTROL_cu_spc), .CU_SPE(CONTROL_cu_spe),
    .CU_SPI(CONTROL_cu_spi), .CU_TXS(CONTROL_cu_txs), .CU_TXO(CONTROL_cu_txo), .CU_AXS(CONTROL_cu_axs),
    .CU_AXO(CONTROL_cu_axo), .CU_AXI(CONTROL_cu_axi), .CU_Flag_C(CONTROL_cu_flag_c),
    .CU_Flag_A(CONTROL_cu_flag_a), .CU_Flag_E(CONTROL_cu_flag_e), .CU_Flag_Z(CONTROL_cu_flag_z),
    .CU_Ready(CONTROL_cu_ready), .CU_Halt(CONTROL_cu_halt), .CU_Clockstep(CONTROL_cu_clockstep));  // open: Flags, IRS, MAE, MDE, MDO, RR, RW, IAS, IAE, PCC, PCE, PCS, PCD, SPC, SPE, SPI, TXS, TXO, AXS, AXO, AXI, ALU_Ops
  LED led_19 (.in(CONTROL_cu_axo));
  LED led_20 (.in(CONTROL_cu_axi));
  Hex_Digit_Display #(.decimalPoint("false")) hex_digit_display_1 (.value(CONTROL_cu_clockstep));
  LED led_21 (.in(CONTROL_cu_ready));
  LED led_22 (.in(CONTROL_cu_halt));
  LED led_23 (.in(CONTROL_cu_flag_c));
  LED led_24 (.in(CONTROL_cu_flag_a));
  LED led_25 (.in(CONTROL_cu_flag_e));
  LED led_26 (.in(CONTROL_cu_flag_z));
endmodule

module ctrs_8_p (
  input  Reset,
  input  Set,
  input  Inc,
  input  Enb,
  input  Clk,
  output [3:0] LED_MSB,
  output [3:0] LED_LSB,
  output [7:0] Q
);

  Counter #(.max('h1f), .width(5)) counter_1 (
    .clr(Reset), .load(Set), .up(Inc), .count(Enb), .clk(Clk), .Q({LED_MSB[0], LED_LSB}));  // open: D, carry

  assign LED_MSB[3:1] = 3'b111;
  assign Q = {3'b111, LED_MSB[0], LED_LSB};
endmodule
